# Fritzing sketch circuit_diagram (saved by Fritzing 0.9.3b)
breadboards: 1

parts:
  Bauteil1 = Arduino Uno (Rev3)
  R1 = Photocell (LDR) [package=THT]
  R2 = Photocell (LDR) [package=THT]
  R3 = Photocell (LDR) [package=THT]
  R4 = Resistor [tolerance=±5% resistance=220 package=THT]
  R5 = Resistor [tolerance=±5% resistance=220 package=THT]
  R6 = Resistor [tolerance=±5% resistance=220 package=THT]
  LED1 = LED - 5mm [color="Infrared (880nm)" package="5 mm [THT]"]
  LED4 = RGB LED (com. cathode, rgb) [package="5 mm [THT]"]
  R7 = Resistor [tolerance=±5% resistance=220 package=THT]
  R8 = Resistor [tolerance=±5% resistance=220 package=THT]
  R10 = Resistor [tolerance=±5% resistance=220 package=THT]
  R11 = Resistor [tolerance=±5% resistance=220 package=THT]
  R12 = Resistor [tolerance=±5% resistance=220 package=THT]
  X1_-_motor_driver1 = X113647 Stepper Driver Board [package=board]
  Schrittmotor1 = 28BYJ-48 Stepper Motor
  X1_-_motor_driver2 = X113647 Stepper Driver Board [package=board]
  Schrittmotor2 = 28BYJ-48 Stepper Motor
  LED3 = LED - 5mm [color="Infrared (880nm)" package="5 mm [THT]"]

nets:
  N1: Bauteil1.A0, R1.pin_0, R6.Pin_1
  N2: Bauteil1.A1, R2.pin_0, R5.Pin_1
  N3: Bauteil1.A2, R3.pin_0, R4.Pin_1
  N4: Bauteil1.D8, X1_-_motor_driver2.IN4
  N5: Bauteil1.D9_PWM, X1_-_motor_driver1.IN1
  N6: Bauteil1.D10_PWM/SS, X1_-_motor_driver1.IN2
  N7: Bauteil1.D11_PWM/MOSI, X1_-_motor_driver1.IN3
  N8: Bauteil1.D12/MISO, X1_-_motor_driver1.IN4
  GND: Bauteil1.GND, R1.pin_1, R2.pin_1, R3.pin_1, LED1.cathode, LED4.common_cathode, X1_-_motor_driver1.GND, X1_-_motor_driver2.GND, LED3.cathode
  N9: Bauteil1.D2, R10.Pin_1
  N10: Bauteil1.D3_PWM, R12.Pin_1
  N11: Bauteil1.D4, R11.Pin_1
  N12: Bauteil1.D5_PWM, X1_-_motor_driver2.IN1
  N13: Bauteil1.D6_PWM, X1_-_motor_driver2.IN2
  N14: Bauteil1.D7, X1_-_motor_driver2.IN3
  N15: Bauteil1.5V, R4.Pin_0, R5.Pin_0, R6.Pin_0, R7.Pin_0, R8.Pin_0, X1_-_motor_driver1.+V, X1_-_motor_driver2.+V
  N16: LED1.anode, R8.Pin_1
  N17: LED4.red_anode, R11.Pin_0
  N18: LED4.green_anode, R12.Pin_0
  N19: LED4.blue_anode, R10.Pin_0
  N20: R7.Pin_1, LED3.anode
  N21: X1_-_motor_driver1.BLUE, Schrittmotor1.BLUE
  N22: X1_-_motor_driver1.PINK, Schrittmotor1.PINK
  N23: X1_-_motor_driver1.YELLOW, Schrittmotor1.YELLOW
  N24: X1_-_motor_driver1.ORANGE, Schrittmotor1.ORANGE
  N25: X1_-_motor_driver1.RED, Schrittmotor1.RED
  N26: X1_-_motor_driver2.BLUE, Schrittmotor2.BLUE
  N27: X1_-_motor_driver2.PINK, Schrittmotor2.PINK
  N28: X1_-_motor_driver2.YELLOW, Schrittmotor2.YELLOW
  N29: X1_-_motor_driver2.ORANGE, Schrittmotor2.ORANGE
  N30: X1_-_motor_driver2.RED, Schrittmotor2.RED

custom parts:
  X113647 Stepper Driver Board: A common stepper motor driver board based on ULN2003APG darlington array
